# Fritzing sketch Gambot (saved by Fritzing 0.9.3b)
breadboards: 1

parts:
  IC1 = IC, DIP package, 40 pins [chip_label=PIC18F45K20]
  Ponte_H = H-Bridge [package=THT]
  Regulador_de_Tensao = Voltage Regulator - 3.3V [package="TO220 [THT]"]
  Motor_direçao = DC Motor
  Motor_principal = DC Motor
  VCC_-_MCU = 4 x AAA Battery Mount
  Analogico_Esq = JOYSTICK-PSP1000 [package=joystick-psp1000]
  VCC_-_motor = Battery block 9V
  Analogico_Dir = JOYSTICK-PSP1000 [package=joystick-psp1000]

nets:
  N1: IC1.pin2, Analogico_Esq.X
  N2: IC1.pin3, Analogico_Dir.Y
  3.3V: IC1.pin11, Ponte_H.1_2EN, Ponte_H.3_4EN, Ponte_H.VCC1, Regulador_de_Tensao.output_voltage, Analogico_Esq.VCC, Analogico_Dir.VCC
  GND: IC1.pin12, Ponte_H.GND1, Ponte_H.GND2, Ponte_H.GND3, Ponte_H.GND4, Regulador_de_Tensao.GND, VCC_-_MCU.-, Analogico_Esq.GND, VCC_-_motor.-, Analogico_Dir.GND
  N3: IC1.pin16, Ponte_H.2A
  N4: IC1.pin17, Ponte_H.1A
  N5: IC1.pin37, Ponte_H.4A
  N6: IC1.pin38, Ponte_H.3A
  N7: Ponte_H.1Y, Motor_principal.pin_1
  N8: Ponte_H.2Y, Motor_principal.pin_2
  N9: Ponte_H.VCC2, VCC_-_motor.+
  N10: Ponte_H.3Y, Motor_direçao.pin_2
  N11: Ponte_H.4Y, Motor_direçao.pin_1
  N12: Regulador_de_Tensao.input_voltage, VCC_-_MCU.+
